// Logisim project SevenSegDec (2).circ as structural Verilog: 1 circuit, main circuit SevenSegDec
module SevenSegDec (
  input  A3,
  input  A2,
  input  A1,
  input  A0,
  output S0,
  output S1,
  output S2,
  output S3,
  output S4,
  output S5,
  output S6
);

  wire and_1_out, and_2_out, and_3_out, and_4_out, and_5_out, and_6_out, and_7_out, and_8_out, and_9_out,
       and_10_out, and_11_out, and_12_out, not_1_out, not_2_out, not_3_out, not_4_out, or_1_out;

  not not_1 (not_1_out, A3);
  not not_2 (not_2_out, A2);
  not not_3 (not_3_out, A1);
  not not_4 (not_4_out, A0);
  and and_1 (and_1_out, not_1_out, not_2_out, not_3_out, not_4_out);
  and and_2 (and_2_out, not_1_out, not_2_out, not_3_out, A0);
  and and_3 (and_3_out, not_1_out, not_2_out, A1, not_4_out);
  and and_4 (and_4_out, not_1_out, not_2_out, A1, A0);
  and and_5 (and_5_out, not_1_out, A2, not_3_out, not_4_out);
  and and_6 (and_6_out, not_1_out, A2, not_3_out, A0);
  and and_7 (and_7_out, not_1_out, A2, A1, A0);
  and and_8 (and_8_out, not_1_out, A2, A1, not_4_out);
  and and_9 (and_9_out, A3, not_2_out, not_3_out, not_4_out);
  and and_10 (and_10_out, A3, not_2_out, not_3_out, A0);
  and and_11 (and_11_out, A3, A2);
  and and_12 (and_12_out, A3, A1);
  or or_1 (or_1_out, and_12_out, and_11_out);
  or or_2 (S0, and_1_out, and_2_out, and_4_out, and_5_out, and_6_out, and_8_out, and_7_out);
  or or_3 (S1, and_1_out, and_2_out, and_3_out, and_5_out, and_6_out, and_8_out, and_7_out, and_9_out, or_1_out);
  or or_4 (S2, and_1_out, and_3_out, and_5_out, and_6_out, and_8_out);
  or or_5 (S3, and_1_out, and_4_out, and_8_out, and_10_out);
  or or_6 (S4, and_1_out, and_2_out, and_3_out, and_4_out, and_5_out, and_6_out, and_7_out, and_10_out, and_9_out, or_1_out);
  or or_7 (S5, and_2_out, and_3_out, and_4_out, and_5_out, and_8_out, and_10_out);
  or or_8 (S6, and_1_out, and_2_out, and_4_out, and_8_out, and_7_out, and_10_out);
  _7_Segment_Display u_7_segment_display_1 (.g(S0), .f(S1), .a(S2), .b(S3), .e(S4), .d(S5), .c(S6));  // open: dp

  // Notes on the sheet:
  //   GREG WOO, 260777364
endmodule
